# Fritzing sketch ForLoop_4LED (saved by Fritzing 0.9.10b)
breadboards: 1

parts:
  Raspberry_Pi_1 = Raspberry Pi 3 [part_number=RPI-3-V1.2]  # not connected
  R1 = Resistor [tolerance=±5% resistance=220 package="2010 [SMD]"]
  R2 = Resistor [tolerance=±5% resistance=220 package="2010 [SMD]"]
  R3 = Resistor [tolerance=±5% resistance=220 package="2010 [SMD]"]
  R4 = Resistor [tolerance=±5% resistance=220 package="2010 [SMD]"]
  LED5 = LEDs [package=led10mm]
  Part1 = Adafruit T-Cobbler Plus [part_number="Adafruit #1989 and #2028"]
  LED6 = LEDs [package=led10mm]
  LED7 = LEDs [package=led10mm]
  LED8 = LEDs [package=led10mm]

nets:
  N1: R1.Pin_0, Part1.GPIO26, LED8.C, LED8.A
  N2: R1.Pin_1, R2.Pin_1, R3.Pin_1, R4.Pin_1, Part1.GND
  N3: R2.Pin_0, Part1.GPIO19, LED7.C, LED7.A
  N4: R3.Pin_0, Part1.GPIO13, LED6.C, LED6.A
  N5: R4.Pin_0, LED5.C, LED5.A, Part1.GPIO6

custom parts:
  Adafruit T-Cobbler Plus: The Raspberry Pi has landed on the Maker World like a 40-GPIO pinned, quad-USB ported, credit card sized bomb of DIY joy. And while you can use most of our great Model B accessories by hooking up our downgrade cable, its probably a good time to upgrade your set up and accessorize using all of the 40 pins. That's why we now carry the Assembled Adafruit Pi T-Cobbler Plus - Breakout + Cable for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
